# Fritzing sketch draft (saved by Fritzing 0.9.4)

parts:
  Pro_Micro3 = SparkFun Pro Micro  # not connected
  U8 = Slide_potentiometer_10k [package=slider]  # not connected
  Part1 = Thumb Joystick  # not connected
  Part3 = Analog Digital MUX Breakout  # not connected
  S33 = Round Pushbutton  # not connected
  S34 = Round Pushbutton  # not connected
  S35 = Round Pushbutton  # not connected
  S36 = Round Pushbutton  # not connected
  S37 = Round Pushbutton  # not connected
  S38 = Round Pushbutton  # not connected
  S39 = Round Pushbutton  # not connected
  S40 = Round Pushbutton  # not connected
  S41 = Round Pushbutton  # not connected
  S42 = Round Pushbutton  # not connected
  S43 = Round Pushbutton  # not connected
  S44 = Round Pushbutton  # not connected
  S45 = Round Pushbutton  # not connected
  S46 = Round Pushbutton  # not connected
  S47 = Round Pushbutton  # not connected
  S48 = Round Pushbutton  # not connected
  S49 = Taiway 100-SP-X-T1 SPDT Miniature Toggle Switch [part_number=100-SP-X-T1-0-0-B1-M2 package=THT]
  S50 = Taiway 100-SP-X-T1 SPDT Miniature Toggle Switch [part_number=100-SP-X-T1-0-0-B1-M2 package=THT]
  S51 = Taiway 100-SP-X-T1 SPDT Miniature Toggle Switch [part_number=100-SP-X-T1-0-0-B1-M2 package=THT]
  S52 = Taiway 100-SP-X-T1 SPDT Miniature Toggle Switch [part_number=100-SP-X-T1-0-0-B1-M2 package=THT]  # not connected
  S53 = Taiway 100-SP-X-T1 SPDT Miniature Toggle Switch [part_number=100-SP-X-T1-0-0-B1-M2 package=THT]  # not connected
  S54 = Taiway 100-SP-X-T1 SPDT Miniature Toggle Switch [part_number=100-SP-X-T1-0-0-B1-M2 package=THT]  # not connected
  S55 = Taiway 100-SP-X-T1 SPDT Miniature Toggle Switch [part_number=100-SP-X-T1-0-0-B1-M2 package=THT]
  S56 = Taiway 100-SP-X-T1 SPDT Miniature Toggle Switch [part_number=100-SP-X-T1-0-0-B1-M2 package=THT]
  Part4 = Analog Digital MUX Breakout  # not connected

nets:
  N1: S49.COM, S50.COM, S51.COM
  N2: S55.COM, S56.COM

notes:
  Pot1
  +5V
  A0
  OTB Pot1
  A1
  A2
  HJoy
  B9
  B10
  B16
  B12
  B11
  B14
  B13
  B15
  B8
  B5
  B6
  B7
  B4
  B3
  B2
  B1
  8
  7
  6
  5
  Multiplexer
  Main Arduino
  9
  SIG
  S3
  S2
  S1
  S0
  C3
  C7
  C15
  C11
  C2
  C6
  C14
  C10
  C1
  C5
  C13
  C9
  C8
  C12
  C0
  C4
  Button Pad
  A3
  SELJoy
  VJoy
  Flap
  Extend
  Retract
  SpeedBrakes
  Gear
  Up
  Down
  HDG
  ALT
  Course
  VS
  Left
  Right
  Speed
  4
  3
  2
  1
  0
  FL up
  FL down
  spb up
  spb down
  gear up
  gear down
  HDG left
  HDG right
  course left
  course right
  ALT up
  ALT down
  VS Up
  VS Down
  SPD up
  SPD down

custom parts:
  SparkFun Pro Micro: The Pro Micro is similar to the Pro Mini except with an ATmega32U4 on board. The USB transceiver inside the 32U4 allows us to add USB connectivity on-board and do away with bulky external USB interface. Based on: https://github.com/unorthodox-engineers/unorthodox-arduino/blob/master/Unorthodox/fritzing/parts/Pro%20Micro.fzpz
  Slide_potentiometer_10k: Slide Potentiometer 10K Linear Module Dual Output for Arduino AVR Electronic Block
